# Fritzing sketch Secuencias Casa (saved by Fritzing 0.9.3b)
breadboards: 1

parts:
  part = Resistor [tolerance=±5% resistance=220 package=THT]
  LED_Porche = LED - 5mm [color="Red (633nm)" package="5 mm [THT]"]
  part_2 = Resistor [tolerance=±5% resistance=220 package=THT]
  LED_Salon = LED - 5mm [color="Blue (505nm)" package="5 mm [THT]"]
  part_3 = Resistor [tolerance=±5% resistance=220 package=THT]
  LED_Cocina = LED - 5mm [color="Blue (505nm)" package="5 mm [THT]"]
  part_4 = Resistor [tolerance=±5% resistance=220 package=THT]
  Jardin = LED - 5mm [color="Green (570nm)" package="5 mm [THT]"]
  part_5 = Arduino Uno (Rev3)

nets:
  N1: part.Pin_0, part_5.D11_PWM/MOSI
  N2: part.Pin_1, LED_Porche.anode
  N3: LED_Porche.cathode, LED_Salon.cathode, LED_Cocina.cathode, Jardin.cathode, part_5.GND
  N4: part_2.Pin_0, part_5.D8
  N5: part_2.Pin_1, LED_Salon.anode
  N6: part_3.Pin_0, part_5.D5_PWM
  N7: part_3.Pin_1, LED_Cocina.anode
  N8: part_4.Pin_0, part_5.D2
  N9: part_4.Pin_1, Jardin.anode
