# Fritzing sketch 3.4_SecuenciaCasa (saved by Fritzing 0.9.3b)
breadboards: 1

parts:
  R1 = Resistor [tolerance=±5% resistance=220 package=THT]
  LED_Dormitorio = LED - 5mm [color="Red (633nm)" package="5 mm [THT]"]
  R2 = Resistor [tolerance=±5% resistance=220 package=THT]
  LED_Salon = LED - 5mm [color="Blue (505nm)" package="5 mm [THT]"]
  R3 = Resistor [tolerance=±5% resistance=220 package=THT]
  LED_Cocina = LED - 5mm [color="Blue (505nm)" package="5 mm [THT]"]
  R4 = Resistor [tolerance=±5% resistance=220 package=THT]
  LED_Entrada = LED - 5mm [color="Green (570nm)" package="5 mm [THT]"]
  Arduino_UNO = Arduino Uno (Rev3)

nets:
  N1: R1.Pin_0, Arduino_UNO.D11_PWM/MOSI
  N2: R1.Pin_1, LED_Dormitorio.anode
  N3: LED_Dormitorio.cathode, LED_Salon.cathode, LED_Cocina.cathode, LED_Entrada.cathode, Arduino_UNO.GND
  N4: R2.Pin_0, Arduino_UNO.D8
  N5: R2.Pin_1, LED_Salon.anode
  N6: R3.Pin_0, Arduino_UNO.D5_PWM
  N7: R3.Pin_1, LED_Cocina.anode
  N8: R4.Pin_0, Arduino_UNO.D2
  N9: R4.Pin_1, LED_Entrada.anode
