# Fritzing sketch 5.4_Termostato base (saved by Fritzing 0.9.3b)
breadboards: 1

parts:
  part = Arduino Uno (Rev3)
  part_2 = TMP36 [package=to-92-kit]
  LED1 = LED - 5mm [color="Green (570nm)" package="5 mm [THT]"]
  R2 = Resistor [tolerance=±5% resistance=220 package=THT]

nets:
  N1: part.A0, part_2.VOUT
  GND: part.GND, part_2.GND, R2.Pin_0
  N2: part.D6_PWM, LED1.anode
  5V: part.5V, part_2.VCC
  N3: LED1.cathode, R2.Pin_1
