# Fritzing sketch Shield_PCB_fase_2 (saved by Fritzing 0.9.3b)
circuit board: 6.84961cm x 5.30306cm
breadboards: 1

parts:
  R1 = Resistor [tolerance=±5% resistance=220 package=THT]
  LED1 = LED - 5mm [color="Red (633nm)" package="5 mm [THT]"]
  LED2 = LED - 5mm [color="Red (633nm)" package="5 mm [THT]"]
  LED3 = LED - 5mm [color="Red (633nm)" package="5 mm [THT]"]
  LED4 = LED - 5mm [color="Red (633nm)" package="5 mm [THT]"]
  R2 = Resistor [tolerance=±5% resistance=220 package=THT]
  R3 = Resistor [tolerance=±5% resistance=220 package=THT]
  R4 = Resistor [tolerance=±5% resistance=220 package=THT]
  R5 = Resistor [tolerance=±5% resistance=220 package=THT]
  LED5 = LED - 5mm [color="Red (633nm)" package="5 mm [THT]"]
  LED6 = LED - 5mm [color="Red (633nm)" package="5 mm [THT]"]
  R6 = Resistor [tolerance=±5% resistance=220 package=THT]
  Componente1 = Arduino Uno (Rev3)

nets:
  N1: R1.Pin_0, R2.Pin_0, R3.Pin_0, R4.Pin_0, R5.Pin_0, R6.Pin_0, Componente1.GND
  N2: R1.Pin_1, LED1.cathode
  N3: LED1.anode, Componente1.D3_PWM
  N4: LED2.cathode, R2.Pin_1
  N5: LED2.anode, Componente1.D5_PWM
  N6: LED3.cathode, R3.Pin_1
  N7: LED3.anode, Componente1.D6_PWM
  N8: LED4.cathode, R4.Pin_1
  N9: LED4.anode, Componente1.D9_PWM
  N10: R5.Pin_1, LED5.cathode
  N11: LED5.anode, Componente1.D10_PWM/SS
  N12: LED6.cathode, R6.Pin_1
  N13: LED6.anode, Componente1.D11_PWM/MOSI
