# Fritzing sketch 4.3_Fritzing-pulsado_zumbador (saved by Fritzing 0.9.3b)
circuit board: 8.46667cm x 5.64444cm
breadboards: 1

parts:
  Componente1 = Arduino Uno (Rev3)
  Zumbador = Piezo Speaker
  R1_10k = Resistor [tolerance=±5% resistance=10k package=THT]
  Pulsador = Pushbutton [package="[THT]"]

nets:
  N1: Componente1.D12/MISO, Componente1.GND, Zumbador.pin1, Zumbador.pin2, R1_10k.Pin_1
  N2: Componente1.D2, R1_10k.Pin_0, Pulsador.Pin_1, Pulsador.Pin_2
  N3: Componente1.5V, Pulsador.Pin_3, Pulsador.Pin_4
